// Logisim project s-mips.circ as structural Verilog: 25 circuits, main circuit S-MIPS Board
module S_MIPS_Board (
  input  DESHABILITAR_DISPATCHER,
  output halt
);

  wire button_1_out, CLK, CS, d_ff_1_q, LCLR, LoadRAM, LoadRAMOn, LW, R_R_W, R_W, ram_dispatcher_1_finished,
       RCS, Reset_out, RST, TTY_EN;
  wire [2:0] KDB;
  wire [3:0] LMask, Mask, ram_1_read_time, ram_1_write_time, RMask;
  wire [6:0] KDB_DATA, TTY_DATA;
  wire [15:0] Addr, LAddr, RAddr;
  wire [31:0] I0, I1, I2, I3, LData, ram_1_data_out_0, ram_1_data_out_1, ram_1_data_out_2, ram_1_data_out_3,
       RI0, RI1, RI2, RI3;

  TTY #(.rows(25), .cols(80)) tty_1 (.data(TTY_DATA), .clk(CLK), .we(TTY_EN), .clr(RST));
  not not_1 (LoadRAMOn, ram_dispatcher_1_finished);
  RAM_Dispatcher ram_dispatcher_1 (
    .WriteTime(ram_1_write_time), .Clock(CLK), .Data(LData), .Address(LAddr), .Mask(LMask),
    .Finished(ram_dispatcher_1_finished), .Write(LW), .CLR(LCLR));
  Keyboard #(.buflen(64)) keyboard_1 (.clk(CLK), .re(KDB[0]), .avail(KDB[2]), .data(KDB_DATA));  // open: clr
  RAM ram_1 (
    .Address(RAddr), .Data_Out_0(ram_1_data_out_0), .Data_Out_1(ram_1_data_out_1),
    .Data_Out_2(ram_1_data_out_2), .Data_Out_3(ram_1_data_out_3), .Data_In_0(RI0), .Data_In_1(RI1),
    .Data_In_2(RI2), .Data_In_3(RI3), .Mask(RMask), .nRead_Write(R_R_W), .Chip_Select(RCS),
    .Read_Time(ram_1_read_time), .Reset(button_1_out), .Write_Time(ram_1_write_time));
  Button button_1 (.out(button_1_out));
  D_Flip_Flop d_ff_1 (.clk(CLK), .D(1'b1), .Q(d_ff_1_q), .reset(Reset_out));  // open: Qn, preset, en
  Button Reset (.out(Reset_out));
  S_MIPS s_mips_1 (
    .Kbd_Enable(KDB[0]), .Address(Addr), .Kbd_Clear(KDB[1]), .Kbd_Available(KDB[2]), .RAM_In_0(I0),
    .Kbd_ASCII_Data(KDB_DATA), .RAM_In_1(I1), .TTY_Enable(TTY_EN), .RAM_In_2(I2), .RAM_In_3(I3),
    .TTY_ASCII_Data(TTY_DATA), .Reset(RST), .RAM_Out_0(ram_1_data_out_0), .Clock(CLK),
    .RAM_Out_1(ram_1_data_out_1), .Stop(halt), .RAM_Out_2(ram_1_data_out_2), .RAM_Out_3(ram_1_data_out_3),
    .Mask(Mask), .Read_Time(ram_1_read_time), .Write_Time(ram_1_write_time), .nRead_Write(R_W),
    .Chip_Select(CS));
  D_Flip_Flop d_ff_2 (.clk(CLK), .D(d_ff_1_q), .Qn(LCLR), .reset(Reset_out));  // open: Q, preset, en
  or or_1 (RST, LCLR, LoadRAM);
  Clock clock_1 (.out(CLK));
  Multiplexer #(.width(32), .enable("false")) multiplexer_1 (.in0(I0), .in1(LData), .out(RI0), .sel(LoadRAM));
  Multiplexer #(.width(32), .enable("false")) multiplexer_2 (.in0(I1), .in1(LData), .out(RI1), .sel(LoadRAM));
  Multiplexer #(.width(32), .enable("false")) multiplexer_3 (.in0(I2), .in1(LData), .out(RI2), .sel(LoadRAM));
  Multiplexer #(.width(32), .enable("false")) multiplexer_4 (.in0(I3), .in1(LData), .out(RI3), .sel(LoadRAM));
  and and_1 (LoadRAM, ~DESHABILITAR_DISPATCHER, LoadRAMOn);  // AND_Gate
  Multiplexer #(.width(16), .enable("false")) multiplexer_5 (.in0(Addr), .in1(LAddr), .out(RAddr), .sel(LoadRAM));
  Multiplexer #(.width(4), .enable("false")) multiplexer_6 (.in0(Mask), .in1(LMask), .out(RMask), .sel(LoadRAM));
  Multiplexer #(.enable("false")) multiplexer_7 (.in0(CS), .in1(LW), .out(RCS), .sel(LoadRAM));
  Multiplexer #(.enable("false")) multiplexer_8 (.in0(R_W), .in1(LW), .out(R_R_W), .sel(LoadRAM));

  // Notes on the sheet:
  //   NO MODIFICAR
  //   Keyboard
endmodule

module RAM (
  input  [15:0] Address,
  input  [31:0] Data_In_0,
  input  [31:0] Data_In_1,
  input  [31:0] Data_In_2,
  input  [31:0] Data_In_3,
  input  [3:0] Mask,
  input  nRead_Write,
  input  Chip_Select,
  input  Reset,
  output [31:0] Data_Out_0,
  output [31:0] Data_Out_1,
  output [31:0] Data_Out_2,
  output [31:0] Data_Out_3,
  output [3:0] Read_Time,
  output [3:0] Write_Time
);

  wire and_2_out, and_3_out, and_4_out, and_5_out, and_6_out, and_7_out, and_8_out, and_9_out, Changed, CLK,
       comparator_2_eq, comparator_3_eq, comparator_4_eq, comparator_5_eq, comparator_6_eq, Count,
       demultiplexer_3_out0, Idle, Idle_q, Load, Load0, Load1, nand_1_out, or_1_out, or_2_out, or_3_out,
       or_4_out, or_5_out, or_6_out, or_7_out, or_8_out, or_9_out, or_10_out, Proc_q, Update_Mem, Zero_Time;
  wire [3:0] counter_1_q, multiplexer_1_out, subtractor_1_out;
  wire [31:0] register_1_q, register_2_q, register_3_q, register_4_q, register_5_q;

  // Probe on 4'b0011
  // Probe on 4'b0010
  Multiplexer #(.width(4), .enable("false")) multiplexer_1 (
    .in0(4'b0011), .in1(4'b0010), .out(multiplexer_1_out), .sel(nRead_Write));
  or or_1 (or_1_out, Idle, Update_Mem);
  or or_2 (or_2_out, ~Chip_Select, Reset);  // OR_Gate
  Subtractor #(.width(4)) subtractor_1 (.a(multiplexer_1_out), .b(4'b0010), .out(subtractor_1_out));  // open: bin, bout
  D_Flip_Flop u_Idle (.clk(CLK), .D(or_1_out), .Q(Idle_q), .preset(or_2_out));  // open: Qn, en, reset
  Demultiplexer #(.enable("false")) demultiplexer_1 (.out0(Idle), .out1(Load0), .in(Idle_q), .sel(Changed));
  // Probe on counter_1_q
  Counter #(.width(4), .max('hf)) counter_1 (
    .load(Load), .D(subtractor_1_out), .count(Count), .Q(counter_1_q), .clk(CLK), .clr(or_3_out));  // open: carry
  or or_3 (or_3_out, ~Chip_Select, Reset);  // OR_Gate
  Comparator #(.width(4), .mode("unsigned")) comparator_1 (
    .a(4'b0000), .b(counter_1_q), .eq(Zero_Time));  // open: gt, lt
  or or_4 (or_4_out, Count, Load0, Load1);
  Register #(.width(32)) register_1 (.D(Data_In_0), .en(Chip_Select), .Q(register_1_q), .clk(CLK), .clr(or_5_out));
  or or_5 (or_5_out, ~Chip_Select, Reset);  // OR_Gate
  Register #(.width(32)) register_2 (.D(Data_In_1), .en(Chip_Select), .Q(register_2_q), .clk(CLK), .clr(or_6_out));
  or or_6 (or_6_out, ~Chip_Select, Reset);  // OR_Gate
  Register #(.width(32)) register_3 (.D(Data_In_2), .en(Chip_Select), .Q(register_3_q), .clk(CLK), .clr(or_7_out));
  or or_7 (or_7_out, ~Chip_Select, Reset);  // OR_Gate
  Register #(.width(32)) register_4 (.D(Data_In_3), .en(Chip_Select), .Q(register_4_q), .clk(CLK), .clr(or_8_out));
  or or_8 (or_8_out, ~Chip_Select, Reset);  // OR_Gate
  Register #(.width(32)) register_5 (
    .D({{11{1'b1}}, nRead_Write, Mask, Address}), .en(Chip_Select), .Q(register_5_q), .clk(CLK),
    .clr(or_9_out));
  or or_9 (or_9_out, ~Chip_Select, Reset);  // OR_Gate
  D_Flip_Flop Proc (.clk(CLK), .D(or_4_out), .Q(Proc_q), .reset(or_10_out));  // open: Qn, preset, en
  or or_10 (or_10_out, ~Chip_Select, Reset);  // OR_Gate
  Demultiplexer #(.enable("false")) demultiplexer_2 (
    .out0(Count), .out1(Update_Mem), .in(demultiplexer_3_out0), .sel(Zero_Time));
  Demultiplexer #(.enable("false")) demultiplexer_3 (
    .out0(demultiplexer_3_out0), .out1(Load1), .in(Proc_q), .sel(Changed));
  Clock clock_1 (.out(CLK));
  Comparator #(.width(32)) comparator_2 (.a(register_1_q), .b(Data_In_0), .eq(comparator_2_eq));  // open: gt, lt
  Comparator #(.width(32)) comparator_3 (.a(register_2_q), .b(Data_In_1), .eq(comparator_3_eq));  // open: gt, lt
  Comparator #(.width(32)) comparator_4 (.a(register_3_q), .b(Data_In_2), .eq(comparator_4_eq));  // open: gt, lt
  Comparator #(.width(32)) comparator_5 (.a(register_4_q), .b(Data_In_3), .eq(comparator_5_eq));  // open: gt, lt
  Comparator #(.width(32)) comparator_6 (
    .a(register_5_q), .b({{11{1'b1}}, nRead_Write, Mask, Address}), .eq(comparator_6_eq));  // open: gt, lt
  nand nand_1 (nand_1_out, comparator_6_eq, comparator_2_eq, comparator_3_eq, comparator_4_eq, comparator_5_eq);
  and and_1 (Changed, nand_1_out, Chip_Select);
  or or_11 (Load, Count, Load1, Load0);
  and and_2 (and_2_out, Mask[0], Update_Mem, nRead_Write);
  and and_3 (and_3_out, Mask[1], Update_Mem, nRead_Write);
  and and_4 (and_4_out, Mask[2], Update_Mem, nRead_Write);
  and and_5 (and_5_out, Mask[3], Update_Mem, nRead_Write);
  RAM_part #(.addrWidth(16), .dataWidth(32), .bus("separate")) ram_1 (
    .addr(Address), .din(Data_In_0), .data(Data_Out_0), .str(and_2_out), .sel(Chip_Select), .clk(CLK),
    .ld(and_6_out), .clr(Reset));
  and and_6 (and_6_out, ~nRead_Write, Idle);  // AND_Gate
  RAM_part #(.addrWidth(16), .dataWidth(32), .bus("separate")) ram_2 (
    .addr(Address), .din(Data_In_1), .data(Data_Out_1), .str(and_3_out), .sel(Chip_Select), .clk(CLK),
    .ld(and_7_out), .clr(Reset));
  and and_7 (and_7_out, ~nRead_Write, Idle);  // AND_Gate
  RAM_part #(.addrWidth(16), .dataWidth(32), .bus("separate")) ram_3 (
    .addr(Address), .din(Data_In_2), .data(Data_Out_2), .str(and_4_out), .sel(Chip_Select), .clk(CLK),
    .ld(and_8_out), .clr(Reset));
  and and_8 (and_8_out, ~nRead_Write, Idle);  // AND_Gate
  RAM_part #(.addrWidth(16), .dataWidth(32), .bus("separate")) ram_4 (
    .addr(Address), .din(Data_In_3), .data(Data_Out_3), .str(and_5_out), .sel(Chip_Select), .clk(CLK),
    .ld(and_9_out), .clr(Reset));
  and and_9 (and_9_out, ~nRead_Write, Idle);  // AND_Gate

  assign Read_Time = 4'b0011;
  assign Write_Time = 4'b0010;

  // Other names for the same wires on the sheet: M0 = Mask[0]; M1 = Mask[1]; M2 = Mask[2]; M3 = Mask[3];
  //   RW = nRead_Write; CLR = Reset; CS = Chip_Select; Load2 = Count

  // Notes on the sheet:
  //   NO MODIFICAR
  //   excepto quizás los valores RT y WT
  //   BANK0
  //   BANK1
  //   BANK2
  //   BANK3
endmodule

module S_MIPS (
  input  Kbd_Available,
  input  [6:0] Kbd_ASCII_Data,
  input  [31:0] RAM_Out_0,
  input  [31:0] RAM_Out_1,
  input  Reset,
  input  [31:0] RAM_Out_2,
  input  Clock,
  input  [31:0] RAM_Out_3,
  input  [3:0] Read_Time,
  input  [3:0] Write_Time,
  output Kbd_Enable,
  output [15:0] Address,
  output Kbd_Clear,
  output TTY_Enable,
  output [6:0] TTY_ASCII_Data,
  output Stop,
  output [31:0] RAM_In_0,
  output [31:0] RAM_In_1,
  output [31:0] RAM_In_2,
  output [31:0] RAM_In_3,
  output [3:0] Mask,
  output nRead_Write,
  output Chip_Select
);

  wire add, addi, ALU_Source, \and , and_1_out, and_2_out, andi, beq, bgtz, blez, bltz, bne, CS___DM,
       CS___MR, d_ff_1_q, d_ff_4_q, demultiplexer_1_out0, demultiplexer_1_out1, demultiplexer_2_out0,
       demultiplexer_2_out1, demultiplexer_3_out0, demultiplexer_3_out1, div, divu, END_Mem, Ext_Selector,
       Finish, halt, jr, jump, kbd, lw, Mem_Access, mfhi, mflo, mult, mulu, nop, \nor , nor_1_out, \or ,
       or_2_out, or_3_out, ori, pop, push, READY, RegDestiny, RegWrite, RI, rnd, RW___DM, RW___MR, slt, slti,
       sltiu, sltu, Stack_Use, Start, sub, sw, tty, Write_Mem, \xor , xori;
  wire [3:0] ALU_Op, RAM_MASK___DM, RAM_MASK___MR;
  wire [4:0] multiplexer_2_out, RD, RS, RT;
  wire [5:0] Func_Code, Op_Code;
  wire [15:0] Const, RAM_A___DM, RAM_A___MR;
  wire [25:0] Destiny_Jump;
  wire [31:0] ALU_Result, branch_control_1_new_direction, Data_Out_Mem, Ext_Const, memory_reader_1_data_out,
       multiplexer_1_out, multiplexer_4_out, New_SP, PC, RD1, RD2, register_file_1_r2, SP;

  or or_1 (Finish, demultiplexer_2_out0, demultiplexer_3_out1);
  Multiplexer #(.width(32), .enable("false")) multiplexer_1 (
    .in0(ALU_Result), .in1(Data_Out_Mem), .out(multiplexer_1_out), .sel(and_1_out));
  and and_1 (and_1_out, Mem_Access, ~Write_Mem);  // AND_Gate
  and and_2 (and_2_out, RegWrite, Finish);
  D_Flip_Flop #(.trigger("falling")) d_ff_1 (
    .clk(Clock), .D(Finish), .Q(d_ff_1_q), .reset(Reset));  // open: Qn, preset, en
  Multiplexer #(.width(5), .enable("false")) multiplexer_2 (
    .in0(RT), .in1(RD), .out(multiplexer_2_out), .sel(RegDestiny));
  D_Flip_Flop #(.trigger("falling")) d_ff_2 (
    .clk(Clock), .D(d_ff_1_q), .Q(Start), .preset(Reset));  // open: Qn, en, reset
  Memory_Selector memory_selector_1 (
    .Selector(nor_1_out), .RAM_A___RM(RAM_A___MR), .RW___MR(RW___MR), .RAM_MASK___MR(RAM_MASK___MR),
    .CS___MR(CS___MR), .RAM_A___DM(RAM_A___DM), .RW___DM(RW___DM), .RAM_MASK___DM(RAM_MASK___DM),
    .CS___DM(CS___DM), .RAM_A(Address), .RW(nRead_Write), .RAM_MASK(Mask), .CS(Chip_Select));
  D_Flip_Flop #(.trigger("falling")) d_ff_3 (.clk(Clock), .D(or_2_out), .Q(RI), .reset(Reset));  // open: Qn, preset, en
  or or_2 (or_2_out, demultiplexer_1_out0, Start);
  nor nor_1 (nor_1_out, Start, RI);
  Register_File register_file_1 (
    .CLK(Clock), .R1(RD1), .RST(Reset), .R_W(and_2_out), .WA(multiplexer_2_out), .R2(register_file_1_r2),
    .RA1(RS), .RA2(RT), .DI(multiplexer_1_out), .NSA(New_SP), .SP(SP));
  Demultiplexer #(.enable("false")) demultiplexer_1 (
    .out0(demultiplexer_1_out0), .out1(demultiplexer_1_out1), .in(RI), .sel(READY));
  Branch_Control branch_control_1 (
    .PC(PC), .Const(Ext_Const), .DestJ(Destiny_Jump), .RT(RD2), .RS(RD1), .beq(beq), .bne(bne), .blez(blez),
    .bgtz(bgtz), .bltz(bltz), .j(jump), .jr(jr), .New_Direction(branch_control_1_new_direction));
  Multiplexer #(.width(32), .enable("false")) multiplexer_3 (
    .in0(register_file_1_r2), .in1(Ext_Const), .out(RD2), .sel(ALU_Source));
  Demultiplexer #(.enable("false")) demultiplexer_2 (
    .out0(demultiplexer_2_out0), .out1(demultiplexer_2_out1), .in(demultiplexer_1_out1), .sel(Mem_Access));
  or or_3 (or_3_out, demultiplexer_3_out0, demultiplexer_2_out1);
  D_Flip_Flop #(.trigger("falling")) d_ff_4 (
    .clk(Clock), .D(or_3_out), .Q(d_ff_4_q), .reset(Reset));  // open: Qn, preset, en
  Demultiplexer #(.enable("false")) demultiplexer_3 (
    .out0(demultiplexer_3_out0), .out1(demultiplexer_3_out1), .in(d_ff_4_q), .sel(END_Mem));
  Program_Counter program_counter_1 (
    .CLK(Clock), .Next_Address(branch_control_1_new_direction), .RST(Reset), .ENB(Finish),
    .Current_Address(PC));
  ALU alu_1 (.A(RD1), .B(RD2), .CLK(Clock), .OP(ALU_Op), .RST(Reset), .ENB(Finish), .Result(ALU_Result));
  Bit_Extender bit_extender_1 (.Const(Const), .Ext_Type(Ext_Selector), .Ext_Const(Ext_Const));
  Memory_Reader memory_reader_1 (
    .Target_Address(PC), .Read_Time(Read_Time), .CLK(Clock), .RST(Reset), .STR(Start), .Input1(RAM_Out_0),
    .Input2(RAM_Out_1), .Input3(RAM_Out_2), .Input4(RAM_Out_3), .Address(RAM_A___MR), .Read_Write(RW___MR),
    .Mask(RAM_MASK___MR), .Chip_Select(CS___MR), .READY(READY), .Data_Out(memory_reader_1_data_out));
  Instruction_Decoder instruction_decoder_1 (
    .Instruction(memory_reader_1_data_out), .div(div), .mult(mult), .jmp(jump), .\nor (\nor ), .add(add),
    .sub(sub), .\xor (\xor ), .\and (\and ), .\or (\or ), .sltu(sltu), .nop(nop), .jr(jr), .mulu(mulu),
    .divu(divu), .mfhi(mfhi), .mflo(mflo), .slt(slt), .ori(ori), .pop(pop), .xori(xori), .addi(addi),
    .push(push), .andi(andi), .beq(beq), .bne(bne), .slti(slti), .sltiu(sltiu), .bltz(bltz), .rnd(rnd),
    .lw(lw), .kbd(kbd), .blez(blez), .halt(halt), .bgtz(bgtz), .tty(tty), .sw(sw), .Op_Code(Op_Code),
    .Destiny_Jump(Destiny_Jump), .RS(RS), .RT(RT), .Const(Const), .RD(RD), .Func_Code(Func_Code));
  Control_Unit control_unit_1 (
    .div(div), .slti(slti), .mult(mult), .sltiu(sltiu), .\nor (\nor ), .rnd(rnd), .add(add), .j(jump),
    .sub(sub), .jr(jr), .\xor (\xor ), .pop(pop), .\and (\and ), .push(push), .\or (\or ), .sltu(sltu),
    .kbd(kbd), .mulu(mulu), .halt(halt), .divu(divu), .tty(tty), .mfhi(mfhi), .beq(beq), .mflo(mflo),
    .bne(bne), .slt(slt), .bltz(bltz), .ori(ori), .lw(lw), .xori(xori), .blez(blez), .addi(addi),
    .bgtz(bgtz), .andi(andi), .sw(sw), .Reg_Write(RegWrite), .ALU_Source(ALU_Source),
    .Reg_Destiny(RegDestiny), .Bit_Extender(Ext_Selector), .ALU_OP(ALU_Op), .nop(\or ),
    .Memory_Access(Mem_Access), .Write_Mem(Write_Mem), .Stack_Use(Stack_Use));
  Multiplexer #(.width(32), .enable("false")) multiplexer_4 (
    .in0(RD2), .in1(RD1), .out(multiplexer_4_out), .sel(Stack_Use));
  Data_Memory data_memory_1 (
    .Target_Address(ALU_Result), .ENB(Mem_Access), .Input1(RAM_Out_0), .Input2(RAM_Out_1),
    .Write_Data(multiplexer_4_out), .Input3(RAM_Out_2), .Input4(RAM_Out_3), .Read_Time(Read_Time),
    .Write_Time(Write_Time), .R_W(Write_Mem), .Clock(Clock), .Reset(Reset), .Address(RAM_A___DM),
    .Chip_Select(CS___DM), .Finish(END_Mem), .Mask(RAM_MASK___DM), .Output1(RAM_In_0), .Output2(RAM_In_1),
    .Data_Out(Data_Out_Mem), .Output3(RAM_In_2), .Output4(RAM_In_3), .push(push), .pop(pop), .R_W_2(RW___DM),
    .SP(SP), .Update_SP(New_SP));

  // Other names for the same wires on the sheet: CLK = Clock; CLR = Reset; CS = Chip_Select;
  //   KBD_AVAIL = Kbd_Available; KBD_CLR = Kbd_Clear; KBD_DATA[6:0] = Kbd_ASCII_Data; RAM_A[15:0] = Address;
  //   RAM_INPUT_0[31:0] = RAM_In_0; RAM_INPUT_1[31:0] = RAM_In_1; RAM_INPUT_2[31:0] = RAM_In_2;
  //   RAM_INPUT_3[31:0] = RAM_In_3; RAM_MASK[3:0] = Mask; RAM_OUTPUT_0[31:0] = RAM_Out_0;
  //   RAM_OUTPUT_1[31:0] = RAM_Out_1; RAM_OUTPUT_2[31:0] = RAM_Out_2; RAM_OUTPUT_3[31:0] = RAM_Out_3;
  //   RW = nRead_Write; TTY_DATA[6:0] = TTY_ASCII_Data

  // Notes on the sheet:
  //   RAM ADDRESS
  //   DATA FROM RAM
  //   DATA TO RAM
  //   DATA WRITE MASK
  //   RAM TIMING
  //   RAM CONTROL
  //   KEYBOARD
  //   TTY
  //   SEQUENCING
  //   Idle
endmodule

module RAM_Dispatcher (
  input  [3:0] WriteTime,
  input  Clock,
  input  CLR,
  output [31:0] Data,
  output [15:0] Address,
  output [3:0] Mask,
  output Finished,
  output Write
);

  wire demultiplexer_2_out1, demultiplexer_3_out1, End, IDLE_q, IncAddr, Load, or_1_out, or_2_out, While_q,
       WriteEnd;
  wire [3:0] counter_1_q;
  wire [31:0] CurrentAddress_q;

  Counter #(.width(32), .max('hffffffff)) CurrentAddress (
    .count(IncAddr), .Q({CurrentAddress_q[31:18], Address, CurrentAddress_q[1:0]}), .clk(Clock), .clr(CLR));  // open: load, D, carry
  or or_1 (or_1_out, IncAddr, demultiplexer_3_out1, Finished);
  D_Flip_Flop IDLE (.clk(Clock), .D(or_1_out), .Q(IDLE_q), .preset(CLR));  // open: Qn, en, reset
  Demultiplexer #(.enable("false")) demultiplexer_1 (.out0(Load), .out1(Finished), .in(IDLE_q), .sel(End));
  D_Flip_Flop While (.clk(Clock), .D(or_2_out), .Q(While_q), .reset(CLR));  // open: Qn, preset, en
  or or_2 (or_2_out, Write, Load);
  RAM_part #(.addrWidth(18), .dataWidth(32)) ram_1 (
    .addr({Address, CurrentAddress_q[1:0]}), .data(Data), .clk(Clock));  // open: sel, ld, clr
  Demultiplexer #(.enable("false")) demultiplexer_2 (
    .out0(Write), .out1(demultiplexer_2_out1), .in(While_q), .sel(WriteEnd));
  Decoder #(.select(2)) decoder_1 (
    .out0(Mask[0]), .out1(Mask[1]), .out2(Mask[2]), .out3(Mask[3]), .sel(CurrentAddress_q[1:0]));  // open: en
  Demultiplexer #(.enable("false")) demultiplexer_3 (
    .out0(IncAddr), .out1(demultiplexer_3_out1), .in(demultiplexer_2_out1), .sel(End));
  Counter #(.width(4), .max('hf)) counter_1 (
    .load(Load), .D(WriteTime), .count(Write), .Q(counter_1_q), .clk(Clock));  // open: carry, clr
  Comparator #(.width(32)) comparator_1 (.a(Data), .b({32{1'b1}}), .eq(End));  // open: gt, lt
  Comparator #(.width(4)) comparator_2 (.a(4'b0000), .b(counter_1_q), .eq(WriteEnd));  // open: gt, lt

  // Other names for the same wires on the sheet: CLK = Clock; Count = Write; WT[3:0] = WriteTime
endmodule

module Register_File (
  input  CLK,
  input  RST,
  input  R_W,
  input  [4:0] WA,
  input  [4:0] RA1,
  input  [4:0] RA2,
  input  [31:0] DI,
  input  [31:0] NSA,
  output [31:0] R1,
  output [31:0] SP,
  output [31:0] R2
);

  wire EN0, EN1, EN2, EN3, EN4, EN5, EN6, EN7, EN8, EN9, EN10, EN11, EN12, EN13, EN14, EN15, EN16, EN17,
       EN18, EN19, EN20, EN21, EN22, EN23, EN24, EN25, EN26, EN27, EN28, EN29, EN30, EN31;
  wire [31:0] register_32_q, S0, S1, S2, S3, S4, S5, S6, S7, S8, S9, S10, S11, S12, S13, S14, S15, S16, S17,
       S18, S19, S20, S21, S22, S23, S24, S25, S26, S27, S28, S29, S30, subtractor_1_out;

  Multiplexer #(.select(5), .width(32)) multiplexer_1 (
    .in0(S0), .in1(S1), .in2(S2), .in3(S3), .in4(S4), .in5(S5), .in6(S6), .in7(S7), .in8(S8), .in9(S9),
    .in10(S10), .in11(S11), .in12(S12), .in13(S13), .in14(S14), .in15(S15), .in16(S16), .in17(S17),
    .in18(S18), .in19(S19), .in20(S20), .in21(S21), .in22(S22), .in23(S23), .in24(S24), .in25(S25),
    .in26(S26), .in27(S27), .in28(S28), .in29(S29), .in30(S30), .in31(SP), .out(R1), .sel(RA1));  // open: en
  Register #(.width(32), .trigger("falling")) register_1 (.D(DI), .en(EN1), .Q(S1), .clk(CLK), .clr(RST));
  Register #(.width(32), .trigger("falling")) register_2 (.D(DI), .en(EN9), .Q(S9), .clk(CLK), .clr(RST));
  Register #(.width(32), .trigger("falling")) register_3 (.D(DI), .en(EN17), .Q(S17), .clk(CLK), .clr(RST));
  Register #(.width(32), .trigger("falling")) register_4 (.D(DI), .en(EN25), .Q(S25), .clk(CLK), .clr(RST));
  // NOT_Gate not_1 has open pins: in=R_W, out=open
  Register #(.width(32)) register_5 (.D({32{1'b0}}), .en(EN0), .Q(S0), .clk(CLK), .clr(RST));
  Register #(.width(32), .trigger("falling")) register_6 (.D(DI), .en(EN2), .Q(S2), .clk(CLK), .clr(RST));
  Register #(.width(32), .trigger("falling")) register_7 (.D(DI), .en(EN10), .Q(S10), .clk(CLK), .clr(RST));
  Register #(.width(32), .trigger("falling")) register_8 (.D(DI), .en(EN18), .Q(S18), .clk(CLK), .clr(RST));
  Register #(.width(32), .trigger("falling")) register_9 (.D(DI), .en(EN26), .Q(S26), .clk(CLK), .clr(RST));
  Register #(.width(32), .trigger("falling")) register_10 (.D(DI), .en(EN3), .Q(S3), .clk(CLK), .clr(RST));
  Register #(.width(32), .trigger("falling")) register_11 (.D(DI), .en(EN11), .Q(S11), .clk(CLK), .clr(RST));
  Register #(.width(32), .trigger("falling")) register_12 (.D(DI), .en(EN19), .Q(S19), .clk(CLK), .clr(RST));
  Register #(.width(32), .trigger("falling")) register_13 (.D(DI), .en(EN27), .Q(S27), .clk(CLK), .clr(RST));
  Demultiplexer #(.select(5), .enable("false")) demultiplexer_1 (
    .out0(EN0), .out1(EN1), .out2(EN2), .out3(EN3), .out4(EN4), .out5(EN5), .out6(EN6), .out7(EN7),
    .out8(EN8), .out9(EN9), .out10(EN10), .out11(EN11), .out12(EN12), .out13(EN13), .out14(EN14),
    .out15(EN15), .out16(EN16), .out17(EN17), .out18(EN18), .out19(EN19), .out20(EN20), .out21(EN21),
    .out22(EN22), .out23(EN23), .out24(EN24), .out25(EN25), .out26(EN26), .out27(EN27), .out28(EN28),
    .out29(EN29), .out30(EN30), .out31(EN31), .in(R_W), .sel(WA));
  Register #(.width(32), .trigger("falling")) register_14 (.D(DI), .en(EN4), .Q(S4), .clk(CLK), .clr(RST));
  Register #(.width(32), .trigger("falling")) register_15 (.D(DI), .en(EN12), .Q(S12), .clk(CLK), .clr(RST));
  Register #(.width(32), .trigger("falling")) register_16 (.D(DI), .en(EN20), .Q(S20), .clk(CLK), .clr(RST));
  Register #(.width(32), .trigger("falling")) register_17 (.D(DI), .en(EN28), .Q(S28), .clk(CLK), .clr(RST));
  Register #(.width(32), .trigger("falling")) register_18 (.D(DI), .en(EN5), .Q(S5), .clk(CLK), .clr(RST));
  Register #(.width(32), .trigger("falling")) register_19 (.D(DI), .en(EN13), .Q(S13), .clk(CLK), .clr(RST));
  Register #(.width(32), .trigger("falling")) register_20 (.D(DI), .en(EN21), .Q(S21), .clk(CLK), .clr(RST));
  Register #(.width(32), .trigger("falling")) register_21 (.D(DI), .en(EN29), .Q(S29), .clk(CLK), .clr(RST));
  Multiplexer #(.select(5), .width(32)) multiplexer_2 (
    .in0(S0), .in1(S1), .in2(S2), .in3(S3), .in4(S4), .in5(S5), .in6(S6), .in7(S7), .in8(S8), .in9(S9),
    .in10(S10), .in11(S11), .in12(S12), .in13(S13), .in14(S14), .in15(S15), .in16(S16), .in17(S17),
    .in18(S18), .in19(S19), .in20(S20), .in21(S21), .in22(S22), .in23(S23), .in24(S24), .in25(S25),
    .in26(S26), .in27(S27), .in28(S28), .in29(S29), .in30(S30), .in31(SP), .out(R2), .sel(RA2));  // open: en
  // NOT_Gate not_2 has open pins: in=R_W, out=open
  Register #(.width(32), .trigger("falling")) register_22 (.D(DI), .en(EN6), .Q(S6), .clk(CLK), .clr(RST));
  Register #(.width(32), .trigger("falling")) register_23 (.D(DI), .en(EN14), .Q(S14), .clk(CLK), .clr(RST));
  Register #(.width(32), .trigger("falling")) register_24 (.D(DI), .en(EN22), .Q(S22), .clk(CLK), .clr(RST));
  Register #(.width(32), .trigger("falling")) register_25 (.D(DI), .en(EN30), .Q(S30), .clk(CLK), .clr(RST));
  Register #(.width(32), .trigger("falling")) register_26 (.D(DI), .en(EN7), .Q(S7), .clk(CLK), .clr(RST));
  Register #(.width(32), .trigger("falling")) register_27 (.D(DI), .en(EN15), .Q(S15), .clk(CLK), .clr(RST));
  Register #(.width(32), .trigger("falling")) register_28 (.D(DI), .en(EN23), .Q(S23), .clk(CLK), .clr(RST));
  Register #(.width(32), .trigger("falling")) register_29 (.D(DI), .en(EN8), .Q(S8), .clk(CLK), .clr(RST));
  Register #(.width(32), .trigger("falling")) register_30 (.D(DI), .en(EN16), .Q(S16), .clk(CLK), .clr(RST));
  Register #(.width(32), .trigger("falling")) register_31 (.D(DI), .en(EN24), .Q(S24), .clk(CLK), .clr(RST));
  Subtractor #(.width(32)) subtractor_1 (.a(32'hffffc), .b(NSA), .out(subtractor_1_out));  // open: bin, bout
  Register #(.width(32), .trigger("falling")) register_32 (
    .D(subtractor_1_out), .en(1'b1), .Q(register_32_q), .clk(CLK), .clr(RST));
  Subtractor #(.width(32)) subtractor_2 (.a(32'hffffc), .b(register_32_q), .out(SP));  // open: bin, bout

  // Other names for the same wires on the sheet: Clock = CLK; Data_Input[31:0] = DI; Next_STk_Address[31:0] = NSA;
  //   Read_Address1[4:0] = RA1; Read_Address2[4:0] = RA2; Read_Ouput1[31:0] = R1; Read_Ouput2[31:0] = R2; Reset = RST;
  //   S31[31:0] = SP; Write_Address[4:0] = WA; Write_Read = R_W
endmodule

module Program_Counter (
  input  CLK,
  input  [31:0] Next_Address,
  input  RST,
  input  ENB,
  output [31:0] Current_Address
);

  Register #(.width(32), .trigger("falling")) register_1 (
    .D(Next_Address), .en(ENB), .Q(Current_Address), .clk(CLK), .clr(RST));

  // Other names for the same wires on the sheet: Clock = CLK; Enable = ENB; Reset = RST
endmodule

module ALU (
  input  [31:0] A,
  input  [31:0] B,
  input  CLK,
  input  [3:0] OP,
  input  RST,
  input  ENB,
  output [31:0] Result
);

  wire comparator_1_lt, comparator_2_lt, High_Low;
  wire [31:0] A_B, A_B_t, A_B_t_t, A_B_t_t_t, A_B_t_t_t_t, A_B_t_t_t_t_t, A_B_t_t_t_t_t_t, A_B_t_t_t_t_t_t_t,
       AvB, High, Low, MFHI, MFLW, multiplexer_1_out, multiplexer_2_out, RNd, US_A_B, US_A_B_t, US_A_B_t_t,
       US_HI_A_B, US_LW_A_B;

  and and_1 (High_Low, OP[2], OP[3]);
  Multiplexer #(.select(2), .width(32)) multiplexer_1 (
    .in0(High), .in1(US_HI_A_B), .in2(A_B), .in3(US_A_B), .out(multiplexer_1_out), .sel(OP[1:0]),
    .en(High_Low));
  Multiplexer #(.select(2), .width(32)) multiplexer_2 (
    .in0(Low), .in1(US_LW_A_B), .in2(A_B_t_t_t), .in3(US_A_B_t), .out(multiplexer_2_out), .sel(OP[1:0]),
    .en(High_Low));
  Adder #(.width(32)) adder_1 (.a(A), .b(B), .out(A_B_t));  // open: cin, cout
  Signed_Division signed_division_1 (.in_1(A), .in_2(B), .Cociente(A_B_t_t_t), .Resto(A_B));
  assign A_B_t_t_t_t_t_t = ~(A | B);  // NOR_Gate nor_1, 32 bits wide
  Register #(.width(32), .trigger("falling")) register_1 (
    .D(multiplexer_1_out), .en(ENB), .Q(MFHI), .clk(CLK), .clr(RST));
  Register #(.width(32), .trigger("falling")) register_2 (
    .D(multiplexer_2_out), .en(ENB), .Q(MFLW), .clk(CLK), .clr(RST));
  Subtractor #(.width(32)) subtractor_1 (.a(A), .b(B), .out(A_B_t_t));  // open: bin, bout
  Divider #(.width(32)) divider_1 (.a(A), .b(B), .out(US_A_B_t), .rem(US_A_B));  // open: upper
  assign A_B_t_t_t_t_t_t_t = A ^ B;  // XOR_Gate xor_1, 32 bits wide
  Random #(.width(32)) random_1 (.clk(CLK), .next(1'b1), .out(RNd));  // open: clr
  Signed_Multiplication signed_multiplication_1 (.in_1(A), .in_2(B), .Low(Low), .High(High));
  assign A_B_t_t_t_t_t = A & B;  // AND_Gate and_2, 32 bits wide
  Comparator #(.width(32)) comparator_1 (.a(A), .b(B), .lt(comparator_1_lt));  // open: gt, eq
  assign A_B_t_t_t_t = {{31{1'b0}}, comparator_1_lt};  // Bit_Extender_part bit_extender_1
  Multiplexer #(.select(4), .width(32), .enable("false")) multiplexer_3 (
    .in0({32{1'b0}}), .in1(A_B_t), .in2(A_B_t_t), .in3(A_B_t_t_t_t_t), .in4(AvB), .in5(A_B_t_t_t_t_t_t),
    .in6(A_B_t_t_t_t_t_t_t), .in7(A_B_t_t_t_t), .in8(US_A_B_t_t), .in9(MFHI), .in10(MFLW), .in11(RNd),
    .in12({32{1'b0}}), .in13({32{1'b0}}), .in14({32{1'b0}}), .in15({32{1'b0}}), .out(Result), .sel(OP));
  Multiplier #(.width(32)) multiplier_1 (.a(A), .b(B), .out(US_LW_A_B), .cout(US_HI_A_B));  // open: cin
  assign AvB = A | B;  // OR_Gate or_1, 32 bits wide
  Comparator #(.width(32), .mode("unsigned")) comparator_2 (.a(A), .b(B), .lt(comparator_2_lt));  // open: gt, eq
  assign US_A_B_t_t = {{31{1'b0}}, comparator_2_lt};  // Bit_Extender_part bit_extender_2

  // Other names for the same wires on the sheet: Clock = CLK; Enable = ENB; Reset = RST
endmodule

module Signed_Multiplication (
  input  [31:0] in_1,
  input  [31:0] in_2,
  output [31:0] Low,
  output [31:0] High
);

  wire not_1_out, Sign;
  wire [31:0] complemento_a2_1_output, complemento_a2_2_output, complementox64_1_high_out,
       complementox64_1_low_out, multiplexer_1_out, multiplexer_2_out, multiplier_1_cout, multiplier_1_out;

  xor xor_1 (Sign, in_1[31], in_2[31]);
  Complemento_A2 complemento_a2_1 (.Input(in_1), .Output(complemento_a2_1_output));
  Complemento_A2 complemento_a2_2 (.Input(in_2), .Output(complemento_a2_2_output));
  Multiplexer #(.width(32), .enable("false")) multiplexer_1 (
    .in0(in_1), .in1(complemento_a2_1_output), .out(multiplexer_1_out), .sel(in_1[31]));
  Multiplexer #(.width(32), .enable("false")) multiplexer_2 (
    .in0(in_2), .in1(complemento_a2_2_output), .out(multiplexer_2_out), .sel(in_2[31]));
  Multiplier #(.width(32)) multiplier_1 (
    .a(multiplexer_1_out), .b(multiplexer_2_out), .out(multiplier_1_out), .cout(multiplier_1_cout));  // open: cin
  ComplementoX64 complementox64_1 (
    .in_1(multiplier_1_out), .in_2(multiplier_1_cout), .High_Out(complementox64_1_high_out),
    .Low_Out(complementox64_1_low_out));
  Multiplexer #(.width(32), .enable("false")) multiplexer_3 (
    .in0(multiplier_1_out), .in1(complementox64_1_low_out), .out(Low), .sel(Sign));
  Multiplexer #(.width(32), .enable("false")) multiplexer_4 (
    .in0(complementox64_1_high_out), .in1(multiplier_1_cout), .out(High), .sel(not_1_out));
  not not_1 (not_1_out, Sign);

  // Other names for the same wires on the sheet: A[31:0] = in_1; B[31:0] = in_2
endmodule

module Complemento_A2 (
  input  [31:0] Input,
  output [31:0] Output
);

  wire [31:0] A;

  assign A = ~Input;  // NOT_Gate not_1, 32 bits wide
  Adder #(.width(32)) adder_1 (.a(A), .b(32'h1), .out(Output));  // open: cin, cout
endmodule

module ComplementoX64 (
  input  [31:0] in_1,
  input  [31:0] in_2,
  output [31:0] Low_Out,
  output [31:0] High_Out
);

  wire adder_1_cout;
  wire [31:0] not_1_out, not_2_out;

  assign not_1_out = ~in_2;  // NOT_Gate not_1, 32 bits wide
  assign not_2_out = ~in_1;  // NOT_Gate not_2, 32 bits wide
  Adder #(.width(32)) adder_1 (.a(not_1_out), .b(32'h1), .out(Low_Out), .cout(adder_1_cout));  // open: cin
  Adder #(.width(32)) adder_2 (.a(not_2_out), .b({32{1'b0}}), .out(High_Out), .cin(adder_1_cout));  // open: cout

  // Other names for the same wires on the sheet: High[31:0] = in_1; Low[31:0] = in_2
endmodule

module Signed_Division (
  input  [31:0] in_1,
  input  [31:0] in_2,
  output [31:0] Cociente,
  output [31:0] Resto
);

  wire Sign;
  wire [31:0] complemento_a2_1_output, complemento_a2_2_output, complemento_a2_3_output,
       complemento_a2_4_output, divider_1_out, divider_1_rem, multiplexer_1_out, multiplexer_2_out;

  xor xor_1 (Sign, in_1[31], in_2[31]);
  Complemento_A2 complemento_a2_1 (.Input(in_1), .Output(complemento_a2_1_output));
  Complemento_A2 complemento_a2_2 (.Input(in_2), .Output(complemento_a2_2_output));
  Multiplexer #(.width(32), .enable("false")) multiplexer_1 (
    .in0(in_1), .in1(complemento_a2_1_output), .out(multiplexer_1_out), .sel(in_1[31]));
  Multiplexer #(.width(32), .enable("false")) multiplexer_2 (
    .in0(in_2), .in1(complemento_a2_2_output), .out(multiplexer_2_out), .sel(in_2[31]));
  Divider #(.width(32)) divider_1 (
    .a(multiplexer_1_out), .b(multiplexer_2_out), .out(divider_1_out), .rem(divider_1_rem));  // open: upper
  Complemento_A2 complemento_a2_3 (.Input(divider_1_out), .Output(complemento_a2_3_output));
  Complemento_A2 complemento_a2_4 (.Input(divider_1_rem), .Output(complemento_a2_4_output));
  Multiplexer #(.width(32), .enable("false")) multiplexer_3 (
    .in0(divider_1_out), .in1(complemento_a2_3_output), .out(Cociente), .sel(Sign));
  Multiplexer #(.width(32), .enable("false")) multiplexer_4 (
    .in0(divider_1_rem), .in1(complemento_a2_4_output), .out(Resto), .sel(Sign));

  // Other names for the same wires on the sheet: A[31:0] = in_1; B[31:0] = in_2
endmodule

module Cicle_Counter (
  input  RESET,
  input  Count,
  input  CLOCK,
  input  [3:0] Read_Time,
  output CHIP_SELECT,
  output READY
);

  wire C, demultiplexer_1_out0, demultiplexer_1_out1, F, IDLE_q, or_1_out, or_2_out, or_3_out;
  wire [3:0] pr;

  or or_1 (or_1_out, demultiplexer_1_out0, F);
  Counter #(.width(4), .max('hf)) counter_1 (.Q(pr), .clk(CLOCK), .clr(or_2_out));  // open: load, D, count, carry
  or or_2 (or_2_out, RESET, IDLE_q);
  Demultiplexer demultiplexer_1 (
    .out0(demultiplexer_1_out0), .out1(demultiplexer_1_out1), .in(IDLE_q), .sel(Count));  // open: en
  D_Flip_Flop IDLE (.clk(CLOCK), .D(or_1_out), .Q(IDLE_q), .preset(RESET));  // open: Qn, en, reset
  or or_3 (or_3_out, demultiplexer_1_out1, C);
  Comparator #(.width(4), .mode("unsigned")) comparator_1 (.a(pr), .b(Read_Time), .eq(READY));  // open: gt, lt
  D_Flip_Flop COUNTING (.clk(CLOCK), .D(or_3_out), .Q(CHIP_SELECT), .reset(RESET));  // open: Qn, preset, en
  Demultiplexer demultiplexer_2 (.out0(C), .out1(F), .in(CHIP_SELECT), .sel(READY));  // open: en

  // Other names for the same wires on the sheet: CLK = CLOCK; CS = CHIP_SELECT; End = READY; RST = RESET;
  //   Time[3:0] = Read_Time
endmodule

module Data_Memory (
  input  [31:0] Target_Address,
  input  push,
  input  pop,
  input  ENB,
  input  [31:0] Input1,
  input  [31:0] Input2,
  input  [31:0] Write_Data,
  input  [31:0] Input3,
  input  [31:0] Input4,
  input  [3:0] Read_Time,
  input  [3:0] Write_Time,
  input  R_W,
  input  Clock,
  input  Reset,
  input  [31:0] SP,
  output [15:0] Address,
  output Chip_Select,
  output Finish,
  output [3:0] Mask,
  output [31:0] Output1,
  output [31:0] Output2,
  output [31:0] Data_Out,
  output [31:0] Output3,
  output [31:0] Output4,
  output R_W_2,
  output [31:0] Update_SP
);

  wire or_1_out;
  wire [3:0] multiplexer_2_out;
  wire [31:0] ADR, multiplexer_3_out, subtractor_1_out, subtractor_2_out;

  Multiplexer #(.select(2), .width(32), .enable("false")) multiplexer_1 (
    .in0(Input1), .in1(Input2), .in2(Input3), .in3(Input4),
    .out({Data_Out[7:0], Data_Out[15:8], Data_Out[23:16], Data_Out[31:24]}), .sel(ADR[3:2]));
  Decoder #(.select(2), .enable("false")) decoder_1 (
    .out0(Mask[0]), .out1(Mask[1]), .out2(Mask[2]), .out3(Mask[3]), .sel(ADR[3:2]));
  Multiplexer #(.width(4), .enable("false")) multiplexer_2 (
    .in0(Read_Time), .in1(Write_Time), .out(multiplexer_2_out), .sel(R_W));
  Cicle_Counter cicle_counter_1 (
    .RESET(Reset), .CHIP_SELECT(Chip_Select), .Count(ENB), .Read_Time(multiplexer_2_out), .READY(Finish),
    .CLOCK(Clock));
  Subtractor #(.width(32)) subtractor_1 (.a(SP), .b(32'h4), .out(subtractor_1_out));  // open: bin, bout
  Multiplexer #(.width(32), .enable("false")) multiplexer_3 (
    .in0(Target_Address), .in1(subtractor_1_out), .out(multiplexer_3_out), .sel(push));
  Multiplexer #(.width(32), .enable("false")) multiplexer_4 (
    .in0(SP), .in1({ADR[31:20], Address, ADR[3:0]}), .out(Update_SP), .sel(or_1_out));
  or or_1 (or_1_out, pop, push);
  Subtractor #(.width(32)) subtractor_2 (.a(SP), .b(32'h4), .out(subtractor_2_out));  // open: bin, bout
  Multiplexer #(.width(32), .enable("false")) multiplexer_5 (
    .in0(multiplexer_3_out), .in1(subtractor_2_out), .out({ADR[31:20], Address, ADR[3:0]}), .sel(pop));

  assign Output1 = {Write_Data[7:0], Write_Data[15:8], Write_Data[23:16], Write_Data[31:24]};
  assign Output2 = {Write_Data[7:0], Write_Data[15:8], Write_Data[23:16], Write_Data[31:24]};
  assign Output3 = {Write_Data[7:0], Write_Data[15:8], Write_Data[23:16], Write_Data[31:24]};
  assign Output4 = {Write_Data[7:0], Write_Data[15:8], Write_Data[23:16], Write_Data[31:24]};
  assign R_W_2 = R_W;

  // Other names for the same wires on the sheet: CS = Chip_Select; Enable = ENB;
  //   NSP[31:0] = {ADR[31:20], Address, ADR[3:0]}; ADR[19:4] = Address; TGA[31:0] = Target_Address
endmodule

module Instruction_Decoder (
  input  [31:0] Instruction,
  output [5:0] Op_Code,
  output div,
  output mult,
  output jmp,
  output [25:0] Destiny_Jump,
  output \nor ,
  output add,
  output sub,
  output [4:0] RS,
  output \xor ,
  output \and ,
  output [4:0] RT,
  output \or ,
  output sltu,
  output [15:0] Const,
  output nop,
  output jr,
  output [4:0] RD,
  output mulu,
  output divu,
  output [5:0] Func_Code,
  output mfhi,
  output mflo,
  output slt,
  output ori,
  output pop,
  output xori,
  output addi,
  output push,
  output andi,
  output beq,
  output bne,
  output slti,
  output sltiu,
  output bltz,
  output rnd,
  output lw,
  output kbd,
  output blez,
  output halt,
  output bgtz,
  output tty,
  output sw
);

  wire and_3_out, R_E, R_N, R_S, Type_R;

  Comparator #(.width(6)) comparator_1 (.a(Instruction[31:26]), .b({6{1'b0}}), .eq(R_N));  // open: gt, lt
  Type_R_Normal type_r_normal_1 (
    .FuncCode(Instruction[5:0]), .enable(R_N), .mult(mult), .div(div), .add(add), .sub(sub), .\nor (\nor ),
    .\xor (\xor ), .\and (\and ), .\or (\or ), .mfhi(mfhi), .mflo(mflo), .slt(slt), .sltu(sltu), .nop(nop),
    .jr(jr), .mulu(mulu), .divu(divu));
  and and_1 (R_S, ~Instruction[26], ~Instruction[27], ~Instruction[28], Instruction[29], Instruction[30], Instruction[31]);  // AND_Gate
  and and_2 (R_E, Instruction[26], Instruction[27], Instruction[28], Instruction[29], Instruction[30], Instruction[31]);
  Type_R_Stack type_r_stack_1 (.FuncCode(Instruction[5:0]), .enable(R_S), .pop(pop), .push(push));
  Type_R_Special type_r_special_1 (
    .Fun_Code(Instruction[5:0]), .enable(R_E), .rnd(rnd), .kbd(kbd), .halt(halt), .tty(tty));
  or or_1 (Type_R, R_N, R_S, R_E);
  and and_3 (and_3_out, ~Type_R, ~jmp);  // AND_Gate
  and and_4 (jmp, ~Instruction[26], Instruction[27], ~Instruction[28], ~Instruction[29], ~Instruction[30], ~Instruction[31]);  // AND_Gate
  Type_I type_i_1 (
    .OpCode(Instruction[31:26]), .enable(and_3_out), .ori(ori), .xori(xori), .addi(addi), .andi(andi),
    .beq(beq), .bne(bne), .slti(slti), .sltiu(sltiu), .bltz(bltz), .lw(lw), .blez(blez), .bgtz(bgtz), .sw(sw));

  assign Const = Instruction[15:0];
  assign Destiny_Jump = Instruction[25:0];
  assign Func_Code = Instruction[5:0];
  assign Op_Code = Instruction[31:26];
  assign RD = Instruction[15:11];
  assign RS = Instruction[25:21];
  assign RT = Instruction[20:16];

  // Other names for the same wires on the sheet: Type_J = jmp
endmodule

module Type_R_Normal (
  input  [5:0] FuncCode,
  input  enable,
  output mult,
  output div,
  output add,
  output sub,
  output \nor ,
  output \xor ,
  output \and ,
  output \or ,
  output mfhi,
  output mflo,
  output slt,
  output sltu,
  output nop,
  output jr,
  output mulu,
  output divu
);

  wire and_1_out, and_3_out, and_5_out, and_7_out, and_9_out, and_11_out, and_13_out, and_14_out, and_17_out,
       and_18_out, and_19_out, and_21_out, and_25_out, and_26_out, and_27_out, and_28_out;

  and and_1 (and_1_out, ~FuncCode[0], ~FuncCode[1], ~FuncCode[2], ~FuncCode[3], ~FuncCode[4], FuncCode[5]);  // AND_Gate
  and and_2 (add, and_1_out, enable);
  and and_3 (and_3_out, ~FuncCode[0], ~FuncCode[1], FuncCode[2], ~FuncCode[3], ~FuncCode[4], FuncCode[5]);  // AND_Gate
  and and_4 (\and , and_3_out, enable);
  and and_5 (and_5_out, ~FuncCode[0], FuncCode[1], ~FuncCode[2], FuncCode[3], ~FuncCode[4], FuncCode[5]);  // AND_Gate
  and and_6 (slt, and_5_out, enable);
  and and_7 (and_7_out, ~FuncCode[0], ~FuncCode[1], ~FuncCode[2], ~FuncCode[3], ~FuncCode[4], ~FuncCode[5]);  // AND_Gate
  and and_8 (nop, and_7_out, enable);
  and and_9 (and_9_out, ~FuncCode[0], FuncCode[1], ~FuncCode[2], ~FuncCode[3], ~FuncCode[4], FuncCode[5]);  // AND_Gate
  and and_10 (sub, and_9_out, enable);
  and and_11 (and_11_out, FuncCode[0], ~FuncCode[1], FuncCode[2], ~FuncCode[3], ~FuncCode[4], FuncCode[5]);  // AND_Gate
  and and_12 (\or , and_11_out, enable);
  and and_13 (and_13_out, FuncCode[0], FuncCode[1], ~FuncCode[2], FuncCode[3], ~FuncCode[4], FuncCode[5]);  // AND_Gate
  and and_14 (and_14_out, ~FuncCode[0], ~FuncCode[1], ~FuncCode[2], FuncCode[3], ~FuncCode[4], ~FuncCode[5]);  // AND_Gate
  and and_15 (sltu, and_13_out, enable);
  and and_16 (jr, and_14_out, enable);
  and and_17 (and_17_out, ~FuncCode[0], ~FuncCode[1], ~FuncCode[2], FuncCode[3], FuncCode[4], ~FuncCode[5]);  // AND_Gate
  and and_18 (and_18_out, ~FuncCode[0], ~FuncCode[1], ~FuncCode[2], ~FuncCode[3], FuncCode[4], ~FuncCode[5]);  // AND_Gate
  and and_19 (and_19_out, FuncCode[0], ~FuncCode[1], ~FuncCode[2], FuncCode[3], FuncCode[4], ~FuncCode[5]);  // AND_Gate
  and and_20 (mult, and_17_out, enable);
  and and_21 (and_21_out, FuncCode[0], FuncCode[1], FuncCode[2], ~FuncCode[3], ~FuncCode[4], FuncCode[5]);  // AND_Gate
  and and_22 (\nor , and_21_out, enable);
  and and_23 (mfhi, and_18_out, enable);
  and and_24 (mulu, and_19_out, enable);
  and and_25 (and_25_out, ~FuncCode[0], FuncCode[1], ~FuncCode[2], FuncCode[3], FuncCode[4], ~FuncCode[5]);  // AND_Gate
  and and_26 (and_26_out, ~FuncCode[0], ~FuncCode[1], ~FuncCode[2], FuncCode[3], ~FuncCode[4], FuncCode[5]);  // AND_Gate
  and and_27 (and_27_out, ~FuncCode[0], FuncCode[1], ~FuncCode[2], ~FuncCode[3], FuncCode[4], ~FuncCode[5]);  // AND_Gate
  and and_28 (and_28_out, FuncCode[0], FuncCode[1], ~FuncCode[2], FuncCode[3], FuncCode[4], ~FuncCode[5]);  // AND_Gate
  and and_29 (div, and_25_out, enable);
  and and_30 (\xor , and_26_out, enable);
  and and_31 (mflo, and_27_out, enable);
  and and_32 (divu, and_28_out, enable);

  // Other names for the same wires on the sheet: en = enable; _0 = FuncCode[0]; _1 = FuncCode[1]; _2 = FuncCode[2];
  //   _3 = FuncCode[3]; _4 = FuncCode[4]; _5 = FuncCode[5]
endmodule

module Type_R_Stack (
  input  [5:0] FuncCode,
  input  enable,
  output pop,
  output push
);

  wire and_1_out, and_3_out;

  and and_1 (and_1_out, ~FuncCode[0], ~FuncCode[1], ~FuncCode[2], ~FuncCode[3], ~FuncCode[4], ~FuncCode[5]);  // AND_Gate
  and and_2 (pop, and_1_out, enable);
  and and_3 (and_3_out, FuncCode[0], ~FuncCode[1], ~FuncCode[2], ~FuncCode[3], ~FuncCode[4], ~FuncCode[5]);  // AND_Gate
  and and_4 (push, and_3_out, enable);

  // Other names for the same wires on the sheet: en = enable; _0 = FuncCode[0]; _1 = FuncCode[1]; _2 = FuncCode[2];
  //   _3 = FuncCode[3]; _4 = FuncCode[4]; _5 = FuncCode[5]
endmodule

module Type_R_Special (
  input  [5:0] Fun_Code,
  input  enable,
  output rnd,
  output kbd,
  output halt,
  output tty
);

  wire and_1_out, and_3_out, and_5_out, and_7_out;

  and and_1 (and_1_out, Fun_Code[0], Fun_Code[1], Fun_Code[2], Fun_Code[3], Fun_Code[5], Fun_Code[5]);
  and and_2 (halt, and_1_out, enable);
  and and_3 (and_3_out, Fun_Code[0], ~Fun_Code[1], ~Fun_Code[2], ~Fun_Code[3], ~Fun_Code[5], ~Fun_Code[5]);  // AND_Gate
  and and_4 (tty, and_3_out, enable);
  and and_5 (and_5_out, ~Fun_Code[0], Fun_Code[1], ~Fun_Code[2], ~Fun_Code[3], ~Fun_Code[5], ~Fun_Code[5]);  // AND_Gate
  and and_6 (rnd, and_5_out, enable);
  and and_7 (and_7_out, ~Fun_Code[0], ~Fun_Code[1], Fun_Code[2], ~Fun_Code[3], ~Fun_Code[5], ~Fun_Code[5]);  // AND_Gate
  and and_8 (kbd, and_7_out, enable);

  assign Fun_Code[4] = Fun_Code[5];

  // Other names for the same wires on the sheet: en = enable; _0 = Fun_Code[0]; _1 = Fun_Code[1]; _2 = Fun_Code[2];
  //   _3 = Fun_Code[3]; _4 = Fun_Code[5]; _5 = Fun_Code[5]
endmodule

module Type_I (
  input  [5:0] OpCode,
  input  enable,
  output ori,
  output xori,
  output addi,
  output andi,
  output beq,
  output bne,
  output slti,
  output sltiu,
  output bltz,
  output lw,
  output blez,
  output bgtz,
  output sw
);

  wire and_1_out, and_2_out, and_3_out, and_4_out, and_9_out, and_11_out, and_13_out, and_15_out, and_16_out,
       and_17_out, and_21_out, and_22_out, and_23_out;

  and and_1 (and_1_out, ~OpCode[0], ~OpCode[1], ~OpCode[2], OpCode[3], ~OpCode[4], ~OpCode[5]);  // AND_Gate
  and and_2 (and_2_out, ~OpCode[0], OpCode[1], ~OpCode[2], OpCode[3], ~OpCode[4], ~OpCode[5]);  // AND_Gate
  and and_3 (and_3_out, ~OpCode[0], OpCode[1], OpCode[2], ~OpCode[3], ~OpCode[4], ~OpCode[5]);  // AND_Gate
  and and_4 (and_4_out, OpCode[0], OpCode[1], ~OpCode[2], OpCode[3], ~OpCode[4], OpCode[5]);  // AND_Gate
  and and_5 (addi, and_1_out, enable);
  and and_6 (slti, and_2_out, enable);
  and and_7 (blez, and_3_out, enable);
  and and_8 (sw, and_4_out, enable);
  and and_9 (and_9_out, ~OpCode[0], ~OpCode[1], OpCode[2], OpCode[3], ~OpCode[4], ~OpCode[5]);  // AND_Gate
  and and_10 (andi, and_9_out, enable);
  and and_11 (and_11_out, OpCode[0], OpCode[1], ~OpCode[2], OpCode[3], ~OpCode[4], ~OpCode[5]);  // AND_Gate
  and and_12 (sltiu, and_11_out, enable);
  and and_13 (and_13_out, OpCode[0], OpCode[1], OpCode[2], ~OpCode[3], ~OpCode[4], ~OpCode[5]);  // AND_Gate
  and and_14 (bgtz, and_13_out, enable);
  and and_15 (and_15_out, OpCode[0], ~OpCode[1], OpCode[2], OpCode[3], ~OpCode[4], ~OpCode[5]);  // AND_Gate
  and and_16 (and_16_out, ~OpCode[0], ~OpCode[1], OpCode[2], ~OpCode[3], ~OpCode[4], ~OpCode[5]);  // AND_Gate
  and and_17 (and_17_out, OpCode[0], ~OpCode[1], ~OpCode[2], ~OpCode[3], ~OpCode[4], ~OpCode[5]);  // AND_Gate
  and and_18 (ori, and_15_out, enable);
  and and_19 (beq, and_16_out, enable);
  and and_20 (bltz, and_17_out, enable);
  and and_21 (and_21_out, ~OpCode[0], OpCode[1], OpCode[2], OpCode[3], ~OpCode[4], ~OpCode[5]);  // AND_Gate
  and and_22 (and_22_out, OpCode[0], ~OpCode[1], OpCode[2], ~OpCode[3], ~OpCode[4], ~OpCode[5]);  // AND_Gate
  and and_23 (and_23_out, OpCode[0], OpCode[1], ~OpCode[2], ~OpCode[3], ~OpCode[4], OpCode[5]);  // AND_Gate
  and and_24 (xori, and_21_out, enable);
  and and_25 (bne, and_22_out, enable);
  and and_26 (lw, and_23_out, enable);

  // Other names for the same wires on the sheet: en = enable; _0 = OpCode[0]; _1 = OpCode[1]; _2 = OpCode[2];
  //   _3 = OpCode[3]; _4 = OpCode[4]; _5 = OpCode[5]
endmodule

module Bit_Extender (
  input  [15:0] Const,
  input  Ext_Type,
  output [31:0] Ext_Const
);

  wire [31:0] bit_extender_1_out, bit_extender_2_out;

  assign bit_extender_1_out = {{16{1'b0}}, Const};  // Bit_Extender_part bit_extender_1
  assign bit_extender_2_out = {{16{Const[15]}}, Const};  // Bit_Extender_part bit_extender_2
  Multiplexer #(.width(32), .enable("false")) multiplexer_1 (
    .in0(bit_extender_1_out), .in1(bit_extender_2_out), .out(Ext_Const), .sel(Ext_Type));

  // Other names for the same wires on the sheet: Extension_Type = Ext_Type
endmodule

module Branch_Control (
  input  [31:0] PC,
  input  [31:0] Const,
  input  [25:0] DestJ,
  input  [31:0] RT,
  input  [31:0] RS,
  input  beq,
  input  bne,
  input  blez,
  input  bgtz,
  input  bltz,
  input  j,
  input  jr,
  output [31:0] New_Direction
);

  wire and_1_out, and_2_out, and_3_out, and_4_out, and_5_out, comparator_2_eq, Condition, Equ, GrtZero,
       LessOrEqualsZero, LessZero, NotEqu, or_3_out;
  wire [31:0] adder_1_out, adder_2_out, Const_t, multiplexer_1_out, multiplexer_2_out;

  Multiplier #(.width(32)) multiplier_1 (.a(Const), .b(32'h4), .out(Const_t));  // open: cin, cout
  and and_1 (and_1_out, beq, Equ);
  and and_2 (and_2_out, bne, NotEqu);
  and and_3 (and_3_out, blez, LessOrEqualsZero);
  and and_4 (and_4_out, bgtz, GrtZero);
  and and_5 (and_5_out, bltz, LessZero);
  Comparator #(.width(32), .mode("unsigned")) comparator_1 (.a(RS), .b(RT), .eq(Equ));  // open: gt, lt
  not not_1 (NotEqu, Equ);
  Comparator #(.width(32), .mode("unsigned")) comparator_2 (
    .a(RS), .b({32{1'b0}}), .gt(GrtZero), .eq(comparator_2_eq), .lt(LessZero));
  or or_1 (Condition, and_1_out, and_2_out, and_3_out, and_4_out, and_5_out);
  or or_2 (LessOrEqualsZero, comparator_2_eq, LessZero);
  Adder #(.width(32)) adder_1 (.a(PC), .b(32'h4), .out(adder_1_out));  // open: cin, cout
  Adder #(.width(32)) adder_2 (.a(adder_1_out), .b(Const_t), .out(adder_2_out));  // open: cin, cout
  Multiplexer #(.width(32), .enable("false")) multiplexer_1 (
    .in0(adder_1_out), .in1(adder_2_out), .out(multiplexer_1_out), .sel(Condition));
  Multiplexer #(.width(32), .enable("false")) multiplexer_2 (
    .in0(RS), .in1({PC[31:28], DestJ, 2'b00}), .out(multiplexer_2_out), .sel(j));
  or or_3 (or_3_out, j, jr);
  Multiplexer #(.width(32), .enable("false")) multiplexer_3 (
    .in0(multiplexer_1_out), .in1(multiplexer_2_out), .out(New_Direction), .sel(or_3_out));

  // Other names for the same wires on the sheet: Destiny_Jump[31:2] = {PC[31:28], DestJ}
endmodule

module Control_Unit (
  input  div,
  input  slti,
  input  mult,
  input  sltiu,
  input  \nor ,
  input  rnd,
  input  add,
  input  j,
  input  sub,
  input  jr,
  input  \xor ,
  input  pop,
  input  \and ,
  input  push,
  input  \or ,
  input  kbd,
  input  nop,
  input  halt,
  input  sltu,
  input  tty,
  input  mulu,
  input  beq,
  input  divu,
  input  bne,
  input  mfhi,
  input  bltz,
  input  mflo,
  input  lw,
  input  slt,
  input  blez,
  input  ori,
  input  bgtz,
  input  xori,
  input  sw,
  input  addi,
  input  andi,
  output Reg_Write,
  output ALU_Source,
  output Reg_Destiny,
  output Bit_Extender,
  output Memory_Access,
  output Write_Mem,
  output Stack_Use,
  output [3:0] ALU_OP
);

  wire or_6_out, or_8_out, or_9_out, or_10_out, or_11_out, or_12_out;

  or or_1 (Reg_Write, pop, add, sub, \and , \or , \xor , \nor , slt, sltu, mfhi, mflo, rnd, addi, slti, sltiu, andi, ori, xori, lw);
  or or_2 (ALU_Source, addi, andi, slti, sltiu, ori, xori);
  or or_3 (Reg_Destiny, pop, add, sub, \and , \or , \xor , slt, sltu, mfhi, mflo, rnd, \nor );
  or or_4 (Memory_Access, pop, push, lw, sw);
  or or_5 (Bit_Extender, addi, slti, sltiu, beq, bne, bltz, blez, bgtz);
  or or_6 (or_6_out, add, lw, sw, addi);
  or or_7 (Stack_Use, pop, push);
  or or_8 (or_8_out, \and , andi);
  or or_9 (or_9_out, \or , ori);
  or or_10 (or_10_out, \xor , xori);
  or or_11 (or_11_out, slt, slti);
  or or_12 (or_12_out, sltu, sltiu);
  or or_13 (Write_Mem, sw, push);
  Priority_Encoder #(.select(4)) priority_encoder_1 (
    .in0(1'b1), .in1(or_6_out), .in2(sub), .in3(or_8_out), .in4(or_9_out), .in5(\nor ), .in6(or_10_out),
    .in7(or_11_out), .in8(or_12_out), .in9(mfhi), .in10(mflo), .in11(rnd), .in12(mult), .in13(mulu),
    .in14(div), .in15(divu), .out(ALU_OP), .en_in(1'b1));  // open: gs, en_out
endmodule

module Memory_Reader (
  input  [31:0] Target_Address,
  input  [3:0] Read_Time,
  input  CLK,
  input  RST,
  input  STR,
  input  [31:0] Input1,
  input  [31:0] Input2,
  input  [31:0] Input3,
  input  [31:0] Input4,
  output [15:0] Address,
  output Read_Write,
  output [3:0] Mask,
  output Chip_Select,
  output READY,
  output [31:0] Data_Out
);

  Multiplexer #(.select(2), .width(32), .enable("false")) multiplexer_1 (
    .in0(Input1), .in1(Input2), .in2(Input3), .in3(Input4),
    .out({Data_Out[7:0], Data_Out[15:8], Data_Out[23:16], Data_Out[31:24]}), .sel(Target_Address[3:2]));
  Decoder #(.select(2), .enable("false")) decoder_1 (
    .out0(Mask[0]), .out1(Mask[1]), .out2(Mask[2]), .out3(Mask[3]), .sel(Target_Address[3:2]));
  Cicle_Counter cicle_counter_1 (
    .RESET(RST), .CHIP_SELECT(Chip_Select), .Count(STR), .Read_Time(Read_Time), .READY(READY), .CLOCK(CLK));

  assign Address = Target_Address[19:4];
  assign Read_Write = 1'b0;

  // Other names for the same wires on the sheet: Clock = CLK; Reset = RST; Start = STR
endmodule

module ALU_Decoder (
  input  div,
  input  mult,
  input  \nor ,
  input  add,
  input  sub,
  input  \xor ,
  input  \and ,
  input  \or ,
  input  sltu,
  input  mulu,
  input  divu,
  input  mfhi,
  input  mflo,
  input  slt,
  input  ori,
  input  xori,
  input  addi,
  input  andi,
  input  slti,
  input  sltiu,
  input  rnd,
  output [3:0] ALU_OP
);

  wire or_1_out, or_2_out, or_3_out, or_4_out, or_5_out, or_6_out;

  or or_1 (or_1_out, add, addi);
  or or_2 (or_2_out, \and , andi);
  or or_3 (or_3_out, \or , ori);
  or or_4 (or_4_out, \xor , xori);
  or or_5 (or_5_out, slt, slti);
  or or_6 (or_6_out, sltu, sltiu);
  Priority_Encoder #(.select(4)) priority_encoder_1 (
    .in0(1'b1), .in1(or_1_out), .in2(sub), .in3(or_2_out), .in4(or_3_out), .in5(\nor ), .in6(or_4_out),
    .in7(or_5_out), .in8(or_6_out), .in9(mfhi), .in10(mflo), .in11(rnd), .in12(mult), .in13(mulu),
    .in14(div), .in15(divu), .out(ALU_OP), .en_in(1'b1));  // open: gs, en_out
endmodule

module crono (
  input  CLCK,
  input  RST,
  input  STR,
  input  [3:0] MEMT,
  output End,
  output Counting
);

  wire comparator_2_eq, d_ff_1_q, not_1_out, or_1_out;
  wire [3:0] counter_1_q;

  Counter #(.width(4), .max('hf)) counter_1 (
    .load(1'b0), .count(STR), .Q(counter_1_q), .clk(CLCK), .clr(or_1_out));  // open: D, carry
  Comparator #(.width(4)) comparator_1 (.a(MEMT), .b(counter_1_q), .eq(End));  // open: gt, lt
  not not_1 (not_1_out, comparator_2_eq);
  Comparator #(.width(4)) comparator_2 (.a(counter_1_q), .b(4'b0000), .eq(comparator_2_eq));  // open: gt, lt
  or or_1 (or_1_out, d_ff_1_q, RST);
  D_Flip_Flop #(.trigger("falling")) d_ff_1 (
    .clk(CLCK), .D(End), .Q(d_ff_1_q), .reset(or_1_out));  // open: Qn, preset, en
  or or_2 (Counting, not_1_out, STR);

  // Other names for the same wires on the sheet: Clock = CLCK; Mem_Time[3:0] = MEMT; Reset = RST; Start = STR
endmodule

module Memory_Selector (
  input  Selector,
  input  [15:0] RAM_A___RM,
  input  RW___MR,
  input  [3:0] RAM_MASK___MR,
  input  CS___MR,
  input  [15:0] RAM_A___DM,
  input  RW___DM,
  input  [3:0] RAM_MASK___DM,
  input  CS___DM,
  output [15:0] RAM_A,
  output RW,
  output [3:0] RAM_MASK,
  output CS
);

  Multiplexer #(.width(16), .enable("false")) multiplexer_1 (
    .in0(RAM_A___RM), .in1(RAM_A___DM), .out(RAM_A), .sel(Selector));
  Multiplexer #(.enable("false")) multiplexer_2 (.in0(RW___MR), .in1(RW___DM), .out(RW), .sel(Selector));
  Multiplexer #(.width(4), .enable("false")) multiplexer_3 (
    .in0(RAM_MASK___MR), .in1(RAM_MASK___DM), .out(RAM_MASK), .sel(Selector));
  Multiplexer #(.enable("false")) multiplexer_4 (.in0(CS___MR), .in1(CS___DM), .out(CS), .sel(Selector));

  // Other names for the same wires on the sheet: RAM_A___MR[15:0] = RAM_A___RM
endmodule
